# Fritzing sketch wiring-diagram (saved by Fritzing 0.9.4)

parts:
  Componente1 = Arduino Uno (Rev3)
  Raspberry_Pi2 = Raspberry Pi B rev2

nets:
  N1: Componente1.A4/SDA, Raspberry_Pi2.GPIO_3
  N2: Componente1.A5/SCL, Raspberry_Pi2.GPIO_2
  GND: Componente1.GND, Raspberry_Pi2.GND
